// Logisim project cpu.circ as structural Verilog: 5 circuits, main circuit main
module main (
  input  [31:0] INSTRUCTION,
  input  CLOCK,
  output [31:0] PROGRAM_COUNTER,
  output [31:0] ra,
  output [31:0] sp,
  output [31:0] t0,
  output [31:0] t1,
  output [31:0] t2,
  output [31:0] s0,
  output [31:0] s1,
  output [31:0] a0
);

  wire areequal, arelessthan, asel, bsel, kill, memRNOTUSED, memW, pcselect, regWEN, tobrch;
  wire [1:0] loadctrls, WBSel;
  wire [3:0] alubits;
  wire [31:0] adder_1_out, adder_2_out, alures, bwritedata, immting, immToMux, mem, memtomux,
       multiplexer_1_out, multiplexer_2_out, multiplexer_3_out, multiplexer_4_out, multiplexer_5_out, pc,
       regAtoBC, subtractor_1_out, writebacc;

  Multiplexer #(.width(32), .enable("false")) multiplexer_1 (
    .in0(PROGRAM_COUNTER), .in1(subtractor_1_out), .out(multiplexer_1_out), .sel(pcselect));
  Subtractor #(.width(32)) subtractor_1 (.a(PROGRAM_COUNTER), .b(32'h4), .out(subtractor_1_out));  // open: bin, bout
  Adder #(.width(32)) adder_1 (.a(PROGRAM_COUNTER), .b(32'h4), .out(adder_1_out));  // open: cin, cout
  Multiplexer #(.width(32), .enable("false")) multiplexer_2 (
    .in0(adder_1_out), .in1(alures), .out(multiplexer_2_out), .sel(pcselect));
  Register #(.width(32)) register_1 (.D(multiplexer_1_out), .en(1'b1), .clk(CLOCK), .Q(pc));  // open: clr
  Register #(.width(32)) u_PC (.D(multiplexer_2_out), .en(1'b1), .clk(CLOCK), .Q(PROGRAM_COUNTER));  // open: clr
  Register #(.width(32)) register_2 (.D(multiplexer_3_out), .en(1'b1), .clk(CLOCK), .Q(immting));  // open: clr
  Multiplexer #(.width(32), .enable("false")) multiplexer_3 (
    .in0(INSTRUCTION), .in1({32{1'b0}}), .out(multiplexer_3_out), .sel(pcselect));
  controlmod controlmod_1 (
    .inputinstr(immting), .brEqual(areequal), .brLessThan(arelessthan), .ALUcontrolbits(alubits),
    .controls({WBSel, memW, memRNOTUSED, asel, bsel, regWEN, pcselect}), .loadcontrols(loadctrls),
    .branchexecuted(kill), .brUn(tobrch));  // open: in_2
  immgen immgen_1 (.in_1(immting), .out_2(immToMux));
  regfile_main RegFile (
    .rs2(immting[24:20]), .rd(immting[11:7]), .Read_Data_1(regAtoBC), .Read_Data_2(bwritedata), .ra(ra),
    .sp(sp), .t0(t0), .t1(t1), .t2(t2), .s0(s0), .s1(s1), .a0(a0), .rs1(immting[19:15]),
    .Write_Data(writebacc), .RegWEn(regWEN), .clk(CLOCK));  // open: in_3
  Multiplexer #(.width(32), .enable("false")) multiplexer_4 (
    .in0(regAtoBC), .in1(pc), .out(multiplexer_4_out), .sel(asel));
  Multiplexer #(.width(32), .enable("false")) multiplexer_5 (
    .in0(bwritedata), .in1(immToMux), .out(multiplexer_5_out), .sel(bsel));
  alu Arithmetic_Logic_Unit (.ALUSel(alubits), .B(multiplexer_5_out), .A(multiplexer_4_out), .Result(alures));
  branchcompare branchcompare_1 (
    .BrUn(tobrch), .regB(bwritedata), .regA(regAtoBC), .equalout(areequal), .lessthanout(arelessthan));
  Adder #(.width(32)) adder_2 (.a(pc), .b(32'h4), .out(adder_2_out));  // open: cin, cout
  Multiplexer #(.select(2), .width(32), .enable("false")) multiplexer_6 (
    .in0(alures), .in1(memtomux), .in2(PROGRAM_COUNTER), .in3(immToMux), .out(writebacc), .sel(WBSel));
  // mem_main DMEM: pin names not known; wires that end beside it: alures, bwritedata, CLOCK, memW, mem
  memload memload_1 (.inputtomem(mem), .loadctrls(loadctrls), .memloadout(memtomux));  // open: in_2, in_3

  // Other names for the same wires on the sheet: clk = CLOCK; rd_1e3999b2[4:0] = immting[11:7];
  //   pcforA[31:0] = PROGRAM_COUNTER; regBtoBC[31:0] = bwritedata

  // Notes on the sheet:
  //   Output
  //   IMEM (do **NOT** move this)
  //   Inputs
  //   Inputs/Outputs for testing. Do **NOT** move these.
endmodule

module immgen (
  input  [31:0] in_1,
  output [31:0] out_2
);

  wire comparator_1_eq, comparator_2_eq, comparator_3_eq, comparator_4_eq, comparator_5_eq, comparator_6_eq;
  wire [2:0] bit_extender_1_out, bit_extender_3_out, bit_extender_4_out, bit_extender_5_out,
       bit_extender_6_out, bit_extender_7_out, choosebranch, choosejal, choosejalr, chooselui,
       multiplier_1_out, multiplier_6_out, or_1_out;
  wire [11:0] adder_1_out, bit_extender_8_out, bit_extender_9_out, shifter_1_out;
  wire [12:0] bit_extender_11_out, bit_extender_12_out, bit_extender_13_out, bit_extender_14_out, or_2_out,
       shifter_2_out, shifter_3_out, shifter_4_out, shifter_5_out;
  wire [20:0] bit_extender_10_out, bit_extender_16_out, bit_extender_17_out, bit_extender_18_out, or_3_out,
       shifter_7_out, shifter_8_out, shifter_9_out, shifter_10_out;
  wire [31:0] bit_extender_15_out, brimm, itype, jalimm, lui, swoffset;

  Comparator #(.width(7), .mode("unsigned")) comparator_1 (
    .a(in_1[6:0]), .b(7'b1100011), .eq(comparator_1_eq));  // open: gt, lt
  Comparator #(.width(7), .mode("unsigned")) comparator_2 (
    .a(in_1[6:0]), .b(7'b1100111), .eq(comparator_2_eq));  // open: gt, lt
  Comparator #(.width(7), .mode("unsigned")) comparator_3 (
    .a(in_1[6:0]), .b(7'b1101111), .eq(comparator_3_eq));  // open: gt, lt
  Comparator #(.width(7), .mode("unsigned")) comparator_4 (
    .a(in_1[6:0]), .b(7'b0110111), .eq(comparator_4_eq));  // open: gt, lt
  assign bit_extender_1_out = {{2{1'b0}}, comparator_5_eq};  // Bit_Extender bit_extender_1
  Comparator #(.width(7), .mode("unsigned")) comparator_5 (
    .a(in_1[6:0]), .b(7'b0001011), .eq(comparator_5_eq));  // open: gt, lt
  Comparator #(.width(7), .mode("unsigned")) comparator_6 (
    .a(in_1[6:0]), .b(7'b0100011), .eq(comparator_6_eq));  // open: gt, lt
  assign itype = {{20{in_1[31]}}, in_1[31:20]};  // Bit_Extender bit_extender_2
  assign bit_extender_3_out = {{2{1'b0}}, comparator_1_eq};  // Bit_Extender bit_extender_3
  assign bit_extender_4_out = {{2{1'b0}}, comparator_2_eq};  // Bit_Extender bit_extender_4
  assign bit_extender_5_out = {{2{1'b0}}, comparator_3_eq};  // Bit_Extender bit_extender_5
  assign bit_extender_6_out = {{2{1'b0}}, comparator_4_eq};  // Bit_Extender bit_extender_6
  Multiplier #(.width(3)) multiplier_1 (.a(bit_extender_1_out), .b(3'b000), .out(multiplier_1_out));  // open: cin, cout
  assign bit_extender_7_out = {{2{1'b0}}, comparator_6_eq};  // Bit_Extender bit_extender_7
  assign bit_extender_8_out = {{7{1'b0}}, in_1[11:7]};  // Bit_Extender bit_extender_8
  assign bit_extender_9_out = {{5{1'b0}}, in_1[31:25]};  // Bit_Extender bit_extender_9
  assign bit_extender_10_out = {{20{1'b0}}, in_1[31]};  // Bit_Extender bit_extender_10
  assign bit_extender_11_out = {{12{1'b0}}, in_1[7]};  // Bit_Extender bit_extender_11
  assign bit_extender_12_out = {{9{1'b0}}, in_1[11:8]};  // Bit_Extender bit_extender_12
  assign bit_extender_13_out = {{7{1'b0}}, in_1[30:25]};  // Bit_Extender bit_extender_13
  assign bit_extender_14_out = {{12{1'b0}}, in_1[31]};  // Bit_Extender bit_extender_14
  Multiplier #(.width(3)) multiplier_2 (.a(bit_extender_3_out), .b(3'b101), .out(choosebranch));  // open: cin, cout
  Multiplier #(.width(3)) multiplier_3 (.a(bit_extender_4_out), .b(3'b100), .out(choosejalr));  // open: cin, cout
  Multiplier #(.width(3)) multiplier_4 (.a(bit_extender_5_out), .b(3'b011), .out(choosejal));  // open: cin, cout
  Multiplier #(.width(3)) multiplier_5 (.a(bit_extender_6_out), .b(3'b010), .out(chooselui));  // open: cin, cout
  Multiplier #(.width(3)) multiplier_6 (.a(bit_extender_7_out), .b(3'b001), .out(multiplier_6_out));  // open: cin, cout
  assign bit_extender_15_out = {{12{1'b0}}, in_1[31:12]};  // Bit_Extender bit_extender_15
  Adder #(.width(12)) adder_1 (.a(bit_extender_8_out), .b(shifter_1_out), .out(adder_1_out));  // open: cin, cout
  Shifter #(.width(12)) shifter_1 (.in(bit_extender_9_out), .\dist (4'b0101), .out(shifter_1_out));
  assign bit_extender_16_out = {{13{1'b0}}, in_1[19:12]};  // Bit_Extender bit_extender_16
  assign bit_extender_17_out = {{20{1'b0}}, in_1[20]};  // Bit_Extender bit_extender_17
  assign bit_extender_18_out = {{11{1'b0}}, in_1[30:21]};  // Bit_Extender bit_extender_18
  Shifter #(.width(13)) shifter_2 (.in(bit_extender_11_out), .\dist (4'b1011), .out(shifter_2_out));
  Shifter #(.width(13)) shifter_3 (.in(bit_extender_12_out), .\dist (4'b0001), .out(shifter_3_out));
  Shifter #(.width(13)) shifter_4 (.in(bit_extender_13_out), .\dist (4'b0101), .out(shifter_4_out));
  Shifter #(.width(13)) shifter_5 (.in(bit_extender_14_out), .\dist (4'b1100), .out(shifter_5_out));
  assign or_1_out = choosebranch | multiplier_1_out | multiplier_6_out | choosejal | choosejalr | chooselui;  // OR_Gate or_1, 3 bits wide
  Shifter #(.width(32)) shifter_6 (.in(bit_extender_15_out), .\dist (5'b01100), .out(lui));
  assign swoffset = {{20{adder_1_out[11]}}, adder_1_out};  // Bit_Extender bit_extender_19
  Shifter #(.width(21)) shifter_7 (.in(bit_extender_16_out), .\dist (5'b01100), .out(shifter_7_out));
  Shifter #(.width(21)) shifter_8 (.in(bit_extender_17_out), .\dist (5'b01011), .out(shifter_8_out));
  Shifter #(.width(21)) shifter_9 (.in(bit_extender_18_out), .\dist (5'b00001), .out(shifter_9_out));
  Shifter #(.width(21)) shifter_10 (.in(bit_extender_10_out), .\dist (5'b10100), .out(shifter_10_out));
  assign or_2_out = shifter_2_out | shifter_3_out | shifter_4_out | shifter_5_out;  // OR_Gate or_2, 13 bits wide
  assign or_3_out = shifter_7_out | shifter_8_out | shifter_9_out | shifter_10_out;  // OR_Gate or_3, 21 bits wide
  assign brimm = {{19{or_2_out[12]}}, or_2_out};  // Bit_Extender bit_extender_20
  Multiplexer #(.select(3), .width(32), .enable("false")) multiplexer_1 (
    .in0(itype), .in1(swoffset), .in2(lui), .in3(jalimm), .in4(itype), .in5(brimm), .out(out_2),
    .sel(or_1_out));  // open: in6, in7
  assign jalimm = {{11{or_3_out[20]}}, or_3_out};  // Bit_Extender bit_extender_21
endmodule

module controlmod (
  input  [31:0] inputinstr,
  input  [3:0] in_2,
  input  brEqual,
  input  brLessThan,
  output [3:0] ALUcontrolbits,
  output [7:0] controls,
  output [1:0] loadcontrols,
  output branchexecuted,
  output brUn
);

  wire comparator_1_eq, comparator_3_eq, comparator_4_eq, comparator_5_eq, comparator_6_eq, comparator_7_eq,
       comparator_8_eq, comparator_9_eq, comparator_10_eq, comparator_11_eq, comparator_12_eq,
       comparator_13_eq, comparator_14_eq, comparator_15_eq, comparator_16_eq, comparator_17_eq,
       comparator_18_eq, comparator_23_eq, comparator_24_eq, comparator_25_eq, comparator_27_eq,
       comparator_28_eq, comparator_29_eq, comparator_30_eq, comparator_31_eq, comparator_32_eq,
       comparator_33_eq, comparator_34_eq, comparator_35_eq, comparator_36_eq, comparator_37_eq,
       comparator_38_eq, comparator_39_eq, four, jalbit, jalrbit, multiplier_20_out, multiplier_21_out,
       multiplier_32_out, multiplier_33_out, not_1_out, not_2_out, one, or_1_out, two;
  wire [1:0] bit_extender_41_out, bit_extender_42_out, bit_extender_43_out, multiplier_36_out,
       multiplier_37_out, multiplier_38_out;
  wire [2:0] or_7_out;
  wire [3:0] bit_extender_5_out, bit_extender_6_out, bit_extender_12_out, bit_extender_13_out,
       bit_extender_14_out, bit_extender_15_out, bit_extender_16_out, bit_extender_17_out,
       bit_extender_18_out, bit_extender_19_out, bit_extender_20_out, bit_extender_21_out,
       bit_extender_22_out, bit_extender_23_out, bit_extender_25_out, bit_extender_26_out,
       bit_extender_27_out, bit_extender_28_out, bit_extender_29_out, bit_extender_30_out,
       bit_extender_31_out, bit_extender_32_out, bit_extender_33_out, bit_extender_34_out,
       bit_extender_35_out, bit_extender_36_out, bit_extender_37_out, bit_extender_38_out,
       bit_extender_39_out, bit_extender_40_out, branchtomux, ctrlforBranch, iload, itype, itypeALU,
       jalrtomux, jaltomux, luitomux, multiplexer_1_out, multiplexer_2_out, multiplexer_3_out,
       multiplexer_4_out, multiplier_3_out, multiplier_4_out, multiplier_5_out, multiplier_6_out,
       multiplier_7_out, multiplier_8_out, multiplier_9_out, multiplier_10_out, multiplier_11_out,
       multiplier_12_out, multiplier_13_out, multiplier_14_out, multiplier_24_out, multiplier_25_out,
       multiplier_26_out, multiplier_27_out, multiplier_28_out, multiplier_29_out, multiplier_30_out,
       multiplier_31_out, multiplier_34_out, multiplier_35_out, muly, or_2_out, or_3_out, or_4_out, or_5_out,
       rtype, rtypeALU, sword;
  wire [9:0] adder_3_out, adder_4_out, bit_extender_1_out, bit_extender_2_out, bit_extender_3_out,
       bit_extender_4_out, bit_extender_7_out, bit_extender_8_out, bit_extender_9_out, bit_extender_10_out,
       functs, loadctrl, shifter_1_out, shifter_2_out, shifter_3_out, shifter_4_out;

  Comparator #(.width(7), .mode("unsigned")) comparator_1 (
    .a(inputinstr[6:0]), .b(7'b1100011), .eq(comparator_1_eq));  // open: gt, lt
  Comparator #(.width(7), .mode("unsigned")) comparator_2 (
    .a(inputinstr[6:0]), .b(7'b1100111), .eq(jalrbit));  // open: gt, lt
  assign bit_extender_1_out = {{7{1'b0}}, inputinstr[14:12]};  // Bit_Extender bit_extender_1
  assign bit_extender_2_out = {{3{1'b0}}, inputinstr[6:0]};  // Bit_Extender bit_extender_2
  assign bit_extender_3_out = {{7{1'b0}}, inputinstr[14:12]};  // Bit_Extender bit_extender_3
  assign bit_extender_4_out = {{3{1'b0}}, inputinstr[31:25]};  // Bit_Extender bit_extender_4
  Shifter #(.width(10)) shifter_1 (.in(bit_extender_4_out), .\dist (4'b0011), .out(shifter_1_out));
  assign bit_extender_5_out = {{3{1'b0}}, comparator_1_eq};  // Bit_Extender bit_extender_5
  assign bit_extender_6_out = {{3{1'b0}}, jalrbit};  // Bit_Extender bit_extender_6
  assign bit_extender_7_out = {{7{1'b0}}, inputinstr[14:12]};  // Bit_Extender bit_extender_7
  assign bit_extender_8_out = {{3{1'b0}}, inputinstr[6:0]};  // Bit_Extender bit_extender_8
  Shifter #(.width(10)) shifter_2 (.in(bit_extender_8_out), .\dist (4'b0011), .out(shifter_2_out));
  assign bit_extender_9_out = {{7{1'b0}}, inputinstr[14:12]};  // Bit_Extender bit_extender_9
  assign bit_extender_10_out = {{3{1'b0}}, inputinstr[31:25]};  // Bit_Extender bit_extender_10
  Shifter #(.width(10)) shifter_3 (.in(bit_extender_2_out), .\dist (4'b0011), .out(shifter_3_out));
  Adder #(.width(10)) adder_1 (.a(bit_extender_3_out), .b(shifter_1_out), .out(functs));  // open: cin, cout
  Multiplier #(.width(4)) multiplier_1 (.a(bit_extender_5_out), .b(4'b0111), .out(branchtomux));  // open: cin, cout
  Multiplier #(.width(4)) multiplier_2 (.a(bit_extender_6_out), .b(4'b0110), .out(jalrtomux));  // open: cin, cout
  Adder #(.width(10)) adder_2 (.a(bit_extender_7_out), .b(shifter_2_out), .out(loadctrl));  // open: cin, cout
  Adder #(.width(10)) adder_3 (.a(bit_extender_9_out), .b(shifter_4_out), .out(adder_3_out));  // open: cin, cout
  Shifter #(.width(10)) shifter_4 (.in(bit_extender_10_out), .\dist (4'b0011), .out(shifter_4_out));
  Adder #(.width(10)) adder_4 (.a(bit_extender_1_out), .b(shifter_3_out), .out(adder_4_out));  // open: cin, cout
  or or_1 (or_1_out, one, two, brUn, four);
  Comparator #(.width(10), .mode("unsigned")) comparator_3 (
    .a({10{1'b0}}), .b(functs), .eq(comparator_3_eq));  // open: gt, lt
  Comparator #(.width(10), .mode("unsigned")) comparator_4 (
    .a(10'h8), .b(functs), .eq(comparator_4_eq));  // open: gt, lt
  Comparator #(.width(10), .mode("unsigned")) comparator_5 (
    .a(10'h100), .b(functs), .eq(comparator_5_eq));  // open: gt, lt
  Comparator #(.width(10), .mode("unsigned")) comparator_6 (
    .a(10'h1), .b(functs), .eq(comparator_6_eq));  // open: gt, lt
  Comparator #(.width(10), .mode("unsigned")) comparator_7 (
    .a(10'hb), .b(functs), .eq(comparator_7_eq));  // open: gt, lt
  Comparator #(.width(10), .mode("unsigned")) comparator_8 (
    .a(10'h2), .b(functs), .eq(comparator_8_eq));  // open: gt, lt
  Comparator #(.width(10), .mode("unsigned")) comparator_9 (
    .a(10'h4), .b(functs), .eq(comparator_9_eq));  // open: gt, lt
  Comparator #(.width(10), .mode("unsigned")) comparator_10 (
    .a(10'hd), .b(functs), .eq(comparator_10_eq));  // open: gt, lt
  Comparator #(.width(10), .mode("unsigned")) comparator_11 (
    .a(10'h6), .b(functs), .eq(comparator_11_eq));  // open: gt, lt
  Comparator #(.width(10), .mode("unsigned")) comparator_12 (
    .a(10'hf), .b(functs), .eq(comparator_12_eq));  // open: gt, lt
  Comparator #(.width(10), .mode("unsigned")) comparator_13 (
    .a(10'h7), .b(functs), .eq(comparator_13_eq));  // open: gt, lt
  Comparator #(.width(10), .mode("unsigned")) comparator_14 (
    .a(10'h5), .b(functs), .eq(comparator_14_eq));  // open: gt, lt
  Comparator #(.width(10), .mode("unsigned")) comparator_15 (.b(functs), .eq(comparator_15_eq));  // open: a, gt, lt
  Comparator #(.width(10), .mode("unsigned")) comparator_16 (.b(functs), .eq(comparator_16_eq));  // open: a, gt, lt
  Comparator #(.width(7), .mode("unsigned")) comparator_17 (
    .a(inputinstr[6:0]), .b(7'b0000011), .eq(comparator_17_eq));  // open: gt, lt
  Comparator #(.width(7), .mode("unsigned")) comparator_18 (
    .a(inputinstr[6:0]), .b(7'b0100011), .eq(comparator_18_eq));  // open: gt, lt
  Comparator #(.width(10), .mode("unsigned")) comparator_19 (.a(10'h318), .b(adder_4_out), .eq(one));  // open: gt, lt
  Comparator #(.width(10), .mode("unsigned")) comparator_20 (.a(adder_4_out), .b(10'h31c), .eq(two));  // open: gt, lt
  Comparator #(.width(10), .mode("unsigned")) comparator_21 (.a(adder_4_out), .b(10'h31e), .eq(brUn));  // open: gt, lt
  Comparator #(.width(10), .mode("unsigned")) comparator_22 (.a(adder_4_out), .b(10'h319), .eq(four));  // open: gt, lt
  assign muly = {{3{1'b0}}, or_1_out};  // Bit_Extender bit_extender_11
  assign bit_extender_12_out = {{3{1'b0}}, comparator_3_eq};  // Bit_Extender bit_extender_12
  assign bit_extender_13_out = {{3{1'b0}}, comparator_4_eq};  // Bit_Extender bit_extender_13
  assign bit_extender_14_out = {{3{1'b0}}, comparator_5_eq};  // Bit_Extender bit_extender_14
  assign bit_extender_15_out = {{3{1'b0}}, comparator_6_eq};  // Bit_Extender bit_extender_15
  assign bit_extender_16_out = {{3{1'b0}}, comparator_7_eq};  // Bit_Extender bit_extender_16
  assign bit_extender_17_out = {{3{1'b0}}, comparator_8_eq};  // Bit_Extender bit_extender_17
  assign bit_extender_18_out = {{3{1'b0}}, comparator_9_eq};  // Bit_Extender bit_extender_18
  assign bit_extender_19_out = {{3{1'b0}}, comparator_10_eq};  // Bit_Extender bit_extender_19
  assign bit_extender_20_out = {{3{1'b0}}, comparator_11_eq};  // Bit_Extender bit_extender_20
  assign bit_extender_21_out = {{3{1'b0}}, comparator_12_eq};  // Bit_Extender bit_extender_21
  assign bit_extender_22_out = {{3{1'b0}}, comparator_13_eq};  // Bit_Extender bit_extender_22
  assign bit_extender_23_out = {{3{1'b0}}, comparator_14_eq};  // Bit_Extender bit_extender_23
  Bit_Extender #(.in_width(1), .out_width(4), .\type ("zero")) bit_extender_24 (.in(comparator_15_eq));  // open: out
  assign bit_extender_25_out = {{3{1'b0}}, comparator_16_eq};  // Bit_Extender bit_extender_25
  Comparator #(.width(7)) comparator_23 (.a(7'b0110011), .b(inputinstr[6:0]), .eq(comparator_23_eq));  // open: gt, lt
  assign bit_extender_26_out = {{3{1'b0}}, comparator_23_eq};  // Bit_Extender bit_extender_26
  Comparator #(.width(7)) comparator_24 (.a(inputinstr[6:0]), .b(7'b0010011), .eq(comparator_24_eq));  // open: gt, lt
  assign bit_extender_27_out = {{3{1'b0}}, comparator_24_eq};  // Bit_Extender bit_extender_27
  assign bit_extender_28_out = {{3{1'b0}}, comparator_17_eq};  // Bit_Extender bit_extender_28
  assign bit_extender_29_out = {{3{1'b0}}, comparator_25_eq};  // Bit_Extender bit_extender_29
  Comparator #(.width(7), .mode("unsigned")) comparator_25 (
    .a(inputinstr[6:0]), .b(7'b0110111), .eq(comparator_25_eq));  // open: gt, lt
  Comparator #(.width(7), .mode("unsigned")) comparator_26 (
    .a(inputinstr[6:0]), .b(7'b1101111), .eq(jalbit));  // open: gt, lt
  Comparator #(.width(3), .mode("unsigned")) comparator_27 (
    .a(3'b000), .b(inputinstr[14:12]), .eq(comparator_27_eq));  // open: gt, lt
  Comparator #(.width(3), .mode("unsigned")) comparator_28 (
    .a(3'b001), .b(inputinstr[14:12]), .eq(comparator_28_eq));  // open: gt, lt
  Comparator #(.width(3), .mode("unsigned")) comparator_29 (
    .a(3'b010), .b(inputinstr[14:12]), .eq(comparator_29_eq));  // open: gt, lt
  Comparator #(.width(3), .mode("unsigned")) comparator_30 (
    .a(3'b100), .b(inputinstr[14:12]), .eq(comparator_30_eq));  // open: gt, lt
  Comparator #(.width(10), .mode("unsigned")) comparator_31 (
    .a(10'h5), .b(adder_3_out), .eq(comparator_31_eq));  // open: gt, lt
  Comparator #(.width(10), .mode("unsigned")) comparator_32 (
    .a(10'h205), .b(adder_3_out), .eq(comparator_32_eq));  // open: gt, lt
  Comparator #(.width(3), .mode("unsigned")) comparator_33 (
    .a(3'b110), .b(inputinstr[14:12]), .eq(comparator_33_eq));  // open: gt, lt
  Comparator #(.width(3), .mode("unsigned")) comparator_34 (
    .a(3'b111), .b(inputinstr[14:12]), .eq(comparator_34_eq));  // open: gt, lt
  Multiplier #(.width(4)) multiplier_3 (
    .a(bit_extender_12_out), .b(4'b0000), .out(multiplier_3_out));  // open: cin, cout
  Multiplier #(.width(4)) multiplier_4 (
    .a(bit_extender_13_out), .b(4'b0001), .out(multiplier_4_out));  // open: cin, cout
  Multiplier #(.width(4)) multiplier_5 (
    .a(bit_extender_14_out), .b(4'b0010), .out(multiplier_5_out));  // open: cin, cout
  Multiplier #(.width(4)) multiplier_6 (
    .a(bit_extender_15_out), .b(4'b0011), .out(multiplier_6_out));  // open: cin, cout
  Multiplier #(.width(4)) multiplier_7 (
    .a(bit_extender_16_out), .b(4'b0100), .out(multiplier_7_out));  // open: cin, cout
  Multiplier #(.width(4)) multiplier_8 (
    .a(bit_extender_17_out), .b(4'b0101), .out(multiplier_8_out));  // open: cin, cout
  Multiplier #(.width(4)) multiplier_9 (
    .a(bit_extender_18_out), .b(4'b0110), .out(multiplier_9_out));  // open: cin, cout
  Multiplier #(.width(4)) multiplier_10 (
    .a(bit_extender_19_out), .b(4'b0111), .out(multiplier_10_out));  // open: cin, cout
  Multiplier #(.width(4)) multiplier_11 (
    .a(bit_extender_20_out), .b(4'b1000), .out(multiplier_11_out));  // open: cin, cout
  Multiplier #(.width(4)) multiplier_12 (
    .a(bit_extender_21_out), .b(4'b1001), .out(multiplier_12_out));  // open: cin, cout
  Multiplier #(.width(4)) multiplier_13 (
    .a(bit_extender_22_out), .b(4'b1010), .out(multiplier_13_out));  // open: cin, cout
  Multiplier #(.width(4)) multiplier_14 (
    .a(bit_extender_23_out), .b(4'b1011), .out(multiplier_14_out));  // open: cin, cout
  Multiplier #(.width(4)) multiplier_15 (.a(bit_extender_25_out), .b(4'b1100));  // open: out, cin, cout
  Multiplier #(.width(4)) multiplier_16 (.a(bit_extender_26_out), .b(4'b0000), .out(rtype));  // open: cin, cout
  Multiplier #(.width(4)) multiplier_17 (.a(bit_extender_27_out), .b(4'b0001), .out(itype));  // open: cin, cout
  Multiplier #(.width(4)) multiplier_18 (.a(bit_extender_28_out), .b(4'b0010), .out(iload));  // open: cin, cout
  assign bit_extender_30_out = {{3{1'b0}}, comparator_18_eq};  // Bit_Extender bit_extender_30
  Multiplier #(.width(4)) multiplier_19 (.a(bit_extender_29_out), .b(4'b0100), .out(luitomux));  // open: cin, cout
  assign bit_extender_31_out = {{3{1'b0}}, jalbit};  // Bit_Extender bit_extender_31
  assign bit_extender_32_out = {{3{1'b0}}, comparator_27_eq};  // Bit_Extender bit_extender_32
  assign bit_extender_33_out = {{3{1'b0}}, comparator_28_eq};  // Bit_Extender bit_extender_33
  assign bit_extender_34_out = {{3{1'b0}}, comparator_29_eq};  // Bit_Extender bit_extender_34
  assign bit_extender_35_out = {{3{1'b0}}, comparator_30_eq};  // Bit_Extender bit_extender_35
  assign bit_extender_36_out = {{3{1'b0}}, comparator_31_eq};  // Bit_Extender bit_extender_36
  assign bit_extender_37_out = {{3{1'b0}}, comparator_32_eq};  // Bit_Extender bit_extender_37
  assign bit_extender_38_out = {{3{1'b0}}, comparator_33_eq};  // Bit_Extender bit_extender_38
  assign bit_extender_39_out = {{3{1'b0}}, comparator_34_eq};  // Bit_Extender bit_extender_39
  Multiplexer #(.width(4), .enable("false")) multiplexer_1 (
    .in0(4'b0000), .in1(4'b0111), .out(multiplexer_1_out), .sel(multiplier_20_out));
  Multiplier #(.width(1)) multiplier_20 (.a(one), .b(brEqual), .out(multiplier_20_out));  // open: cin, cout
  Multiplier #(.width(1)) multiplier_21 (.a(two), .b(brLessThan), .out(multiplier_21_out));  // open: cin, cout
  not not_1 (not_1_out, brEqual);
  Multiplier #(.width(4)) multiplier_22 (.a(bit_extender_30_out), .b(4'b0011), .out(sword));  // open: cin, cout
  Multiplier #(.width(4)) multiplier_23 (.a(bit_extender_31_out), .b(4'b0101), .out(jaltomux));  // open: cin, cout
  Multiplier #(.width(4)) multiplier_24 (
    .a(bit_extender_32_out), .b(4'b0000), .out(multiplier_24_out));  // open: cin, cout
  Multiplier #(.width(4)) multiplier_25 (
    .a(bit_extender_33_out), .b(4'b0001), .out(multiplier_25_out));  // open: cin, cout
  Multiplier #(.width(4)) multiplier_26 (
    .a(bit_extender_34_out), .b(4'b0010), .out(multiplier_26_out));  // open: cin, cout
  Multiplier #(.width(4)) multiplier_27 (
    .a(bit_extender_35_out), .b(4'b0011), .out(multiplier_27_out));  // open: cin, cout
  Multiplier #(.width(4)) multiplier_28 (
    .a(bit_extender_36_out), .b(4'b0100), .out(multiplier_28_out));  // open: cin, cout
  Multiplier #(.width(4)) multiplier_29 (
    .a(bit_extender_37_out), .b(4'b0101), .out(multiplier_29_out));  // open: cin, cout
  Multiplier #(.width(4)) multiplier_30 (
    .a(bit_extender_38_out), .b(4'b0110), .out(multiplier_30_out));  // open: cin, cout
  Multiplier #(.width(4)) multiplier_31 (
    .a(bit_extender_39_out), .b(4'b0111), .out(multiplier_31_out));  // open: cin, cout
  Multiplexer #(.width(4), .enable("false")) multiplexer_2 (
    .in0(4'b0000), .in1(4'b1000), .out(multiplexer_2_out), .sel(multiplier_21_out));
  Multiplier #(.width(1)) multiplier_32 (.a(brUn), .b(brLessThan), .out(multiplier_32_out));  // open: cin, cout
  Multiplier #(.width(1)) multiplier_33 (.a(four), .b(not_1_out), .out(multiplier_33_out));  // open: cin, cout
  Multiplexer #(.width(4), .enable("false")) multiplexer_3 (
    .in0(4'b0000), .in1(4'b1001), .out(multiplexer_3_out), .sel(multiplier_32_out));
  Multiplexer #(.width(4), .enable("false")) multiplexer_4 (
    .in0(4'b0000), .in1(4'b1010), .out(multiplexer_4_out), .sel(multiplier_33_out));
  assign or_2_out = multiplier_3_out | multiplier_4_out | multiplier_5_out | multiplier_6_out | multiplier_7_out | multiplier_8_out | multiplier_9_out | multiplier_10_out | multiplier_11_out | multiplier_12_out | multiplier_13_out | multiplier_14_out;  // OR_Gate or_2, 4 bits wide
  Multiplexer #(.select(4), .width(8), .enable("false")) multiplexer_5 (
    .in0(8'h12), .in1(8'h16), .in2(8'h46), .in3(8'h24), .in4(8'hc2), .in5(8'h8f), .in6(8'h87), .in7(8'hd),
    .in8(8'hd), .in9(8'hd), .in10(8'hd), .in15({8{1'b0}}), .out(controls), .sel(or_5_out));  // open: in11, in12, in13, in14
  assign or_3_out = multiplier_24_out | multiplier_25_out | multiplier_26_out | multiplier_27_out | multiplier_28_out | multiplier_29_out | multiplier_30_out | multiplier_31_out;  // OR_Gate or_3, 4 bits wide
  assign or_4_out = multiplexer_1_out | multiplexer_2_out | multiplexer_3_out | multiplexer_4_out;  // OR_Gate or_4, 4 bits wide
  Multiplexer #(.select(4), .width(4), .enable("false")) multiplexer_6 (
    .in0(4'b0000), .in1(4'b1010), .in2(4'b1100), .in3(4'b0110), .in4(4'b1011), .in5(4'b0111), .in6(4'b0011),
    .in7(4'b1000), .in8(4'b0010), .in9(4'b1001), .in10(4'b0001), .in11(4'b0100), .out(rtypeALU),
    .sel(or_2_out));  // open: in12, in13, in14, in15
  Multiplier #(.width(4)) multiplier_34 (.a(muly), .b(ctrlforBranch), .out(multiplier_34_out));  // open: cin, cout
  Comparator #(.width(4), .mode("unsigned")) comparator_35 (
    .a(or_4_out), .b(4'b0000), .eq(comparator_35_eq));  // open: gt, lt
  Comparator #(.width(4), .mode("unsigned")) comparator_36 (
    .a(or_4_out), .b(4'b0000), .eq(comparator_36_eq));  // open: gt, lt
  assign or_5_out = luitomux | rtype | itype | jalrtomux | iload | sword | jaltomux | multiplier_34_out;  // OR_Gate or_5, 4 bits wide
  Comparator #(.width(10), .mode("unsigned")) comparator_37 (
    .a(10'h18), .b(loadctrl), .eq(comparator_37_eq));  // open: gt, lt
  Comparator #(.width(10), .mode("unsigned")) comparator_38 (
    .a(10'h19), .b(loadctrl), .eq(comparator_38_eq));  // open: gt, lt
  Comparator #(.width(10), .mode("unsigned")) comparator_39 (
    .a(10'h1a), .b(loadctrl), .eq(comparator_39_eq));  // open: gt, lt
  Multiplexer #(.select(4), .width(4), .enable("false")) multiplexer_7 (
    .in0(4'b0000), .in1(4'b0110), .in2(4'b0111), .in3(4'b0011), .in4(4'b1011), .in5(4'b0111), .in6(4'b0010),
    .in7(4'b0001), .out(itypeALU), .sel(or_3_out));  // open: in8, in9, in10, in11, in12, in13, in14, in15
  not not_2 (not_2_out, comparator_35_eq);
  assign bit_extender_40_out = {{3{1'b0}}, comparator_36_eq};  // Bit_Extender bit_extender_40
  assign bit_extender_41_out = {{1{1'b0}}, comparator_37_eq};  // Bit_Extender bit_extender_41
  assign bit_extender_42_out = {{1{1'b0}}, comparator_38_eq};  // Bit_Extender bit_extender_42
  assign bit_extender_43_out = {{1{1'b0}}, comparator_39_eq};  // Bit_Extender bit_extender_43
  or or_6 (branchexecuted, jalbit, jalrbit, not_2_out);
  Multiplier #(.width(4)) multiplier_35 (
    .a(bit_extender_40_out), .b(4'b1111), .out(multiplier_35_out));  // open: cin, cout
  Multiplexer #(.select(3), .width(4), .enable("false")) multiplexer_8 (
    .in0(rtypeALU), .in1(itypeALU), .in2(4'b0000), .in3(4'b0000), .in5(4'b0000), .in6(4'b0000),
    .in7(4'b0000), .out(ALUcontrolbits), .sel(or_7_out));  // open: in4
  assign or_7_out = itype[2:0] | rtype[2:0] | iload[2:0] | sword[2:0] | luitomux[2:0] | jalrtomux[2:0] | branchtomux[2:0];  // OR_Gate or_7, 3 bits wide
  Multiplier #(.width(2)) multiplier_36 (
    .a(bit_extender_41_out), .b(2'b00), .out(multiplier_36_out));  // open: cin, cout
  Multiplier #(.width(2)) multiplier_37 (
    .a(bit_extender_42_out), .b(2'b01), .out(multiplier_37_out));  // open: cin, cout
  Multiplier #(.width(2)) multiplier_38 (
    .a(bit_extender_43_out), .b(2'b10), .out(multiplier_38_out));  // open: cin, cout
  Adder #(.width(4)) adder_5 (.a(or_4_out), .b(multiplier_35_out), .out(ctrlforBranch));  // open: cin, cout
  assign loadcontrols = multiplier_36_out | multiplier_37_out | multiplier_38_out;  // OR_Gate or_8, 2 bits wide

  // Other names for the same wires on the sheet: eqtun = brEqual; funtsItype[2:0] = inputinstr[14:12];
  //   lessthantun = brLessThan; three = brUn

  // Notes on the sheet:
  //   upper bits funct7 lower bits funct3
  //   upper bits funct7 lower bits funct3
  //   upper bits funct7 lower bits funct3
  //   sub
  //   mulhu
  //   slt
  //   xor
  //   divu
  //   or
  //   remu
  //   and
  //   srl
  //   upper bits funct7 lower bits funct3
  //   bltu
  //   add
  //   mul
  //   sll
  //   r control
  //   slt
  //   ori
  //   andi
  //   beq
  //   blt
  //   bne
  //   addi
  //   slli
  //   slti
  //   xori
  //   mulhu
  //   control bits 4 alu
endmodule

module memload (
  input  [31:0] inputtomem,
  input  [1:0] in_2,
  input  in_3,
  input  [1:0] loadctrls,
  output [31:0] memloadout
);

  wire [7:0] bitselector_1_out;
  wire [15:0] bitselector_2_out;
  wire [31:0] bit_extender_1_out, bit_extender_2_out;

  BitSelector #(.width(32), .group(8)) bitselector_1 (.in(inputtomem), .out(bitselector_1_out), .sel(in_2));
  BitSelector #(.width(32), .group(16)) bitselector_2 (.in(inputtomem), .out(bitselector_2_out), .sel(in_3));
  assign bit_extender_1_out = {{24{bitselector_1_out[7]}}, bitselector_1_out};  // Bit_Extender bit_extender_1
  assign bit_extender_2_out = {{16{bitselector_2_out[15]}}, bitselector_2_out};  // Bit_Extender bit_extender_2
  Multiplexer #(.select(2), .width(32), .enable("false")) multiplexer_1 (
    .in0(bit_extender_1_out), .in1(bit_extender_2_out), .in2(inputtomem), .out(memloadout), .sel(loadctrls));  // open: in3
endmodule

module branchcompare (
  input  BrUn,
  input  [31:0] regB,
  input  [31:0] regA,
  output equalout,
  output lessthanout
);

  wire comparator_1_lt, comparator_2_lt;

  Comparator #(.width(32), .mode("unsigned")) comparator_1 (.a(regA), .b(regB), .lt(comparator_1_lt));  // open: gt, eq
  Comparator #(.width(32)) comparator_2 (.a(regA), .b(regB), .lt(comparator_2_lt));  // open: gt, eq
  Comparator #(.width(32)) comparator_3 (.a(regA), .b(regB), .eq(equalout));  // open: gt, lt
  Multiplexer #(.enable("false")) multiplexer_1 (
    .in0(comparator_2_lt), .in1(comparator_1_lt), .out(lessthanout), .sel(BrUn));

  // Notes on the sheet:
  //   unsigned
  //   signed
endmodule
