// Logisim project cpu.circ as structural Verilog: 2 circuits, main circuit main
module main (
  input  [31:0] INSTRUCTION,
  input  CLOCK,
  output [31:0] PROGRAM_COUNTER,
  output [31:0] ra,
  output [31:0] sp,
  output [31:0] t0,
  output [31:0] t1,
  output [31:0] t2,
  output [31:0] s0,
  output [31:0] s1,
  output [31:0] a0
);

  wire [4:0] rd_;
  wire [11:0] immting;
  wire [19:0] register_2_q;
  wire [31:0] adder_1_out, adder_2_out, Arithmetic_Logic_Unit_result, immgen_1_out_2, mem, pc,
       RegFile_read_data_1, writebacc;

  Adder #(.width(32)) adder_1 (.a(PROGRAM_COUNTER), .b(32'h4), .out(adder_1_out));  // open: cin, cout
  Register #(.width(32)) register_1 (.D(PROGRAM_COUNTER), .clk(CLOCK), .Q(pc));  // open: en, clr
  Register #(.width(32)) u_PC (.D(adder_1_out), .clk(CLOCK), .Q(PROGRAM_COUNTER));  // open: en, clr
  Register #(.width(32)) register_2 (
    .D(INSTRUCTION), .clk(CLOCK), .Q({immting, register_2_q[19:12], rd_, register_2_q[6:0]}));  // open: en, clr
  immgen immgen_1 (.in_1(immting), .out_2(immgen_1_out_2));
  regfile_main RegFile (
    .rd(rd_), .Read_Data_1(RegFile_read_data_1), .ra(ra), .sp(sp), .t0(t0), .t1(t1), .t2(t2), .s0(s0),
    .s1(s1), .a0(a0), .rs1(register_2_q[19:15]), .Write_Data(writebacc), .RegWEn(1'b1), .clk(CLOCK));  // open: rs2, Read_Data_2, in_3
  alu Arithmetic_Logic_Unit (
    .ALUSel(4'b0000), .B(immgen_1_out_2), .A(RegFile_read_data_1), .Result(Arithmetic_Logic_Unit_result));
  Multiplexer #(.select(2), .width(32), .enable("false")) multiplexer_1 (
    .in0(Arithmetic_Logic_Unit_result), .in1(mem), .in2(adder_2_out), .out(writebacc), .sel(2'b00));  // open: in3
  Adder #(.width(32)) adder_2 (.a(pc), .b(32'h4), .out(adder_2_out));  // open: cin, cout
  mem_main DMEM (.Read_Data(mem));  // open: Address, Write_Data, Write_En, clk, Read_En

  // Other names for the same wires on the sheet: clk = CLOCK

  // Notes on the sheet:
  //   Output
  //   IMEM (do **NOT** move this)
  //   Inputs
  //   It is OK to move the PC, RegFile, ALU, and MEM to wherever is most convenient for you when constructing your CPU, and to delete this text
  //   Inputs/Outputs for testing. Do **NOT** move these.
endmodule

module immgen (
  input  [11:0] in_1,
  output [31:0] out_2
);

  assign out_2 = {{20{in_1[11]}}, in_1};  // Bit_Extender bit_extender_1
endmodule
