// Logisim project alu.circ as structural Verilog: 1 circuit, main circuit alu
module alu (
  input  [31:0] A,
  input  [31:0] B,
  input  [3:0] ALUSel,
  output [31:0] Result
);

  wire and_2_out, comparator_1_eq, comparator_1_gt, comparator_1_lt, not_1_out, or_2_out;
  wire [31:0] a_t, add0, b_t, c, d, e, f, g, h, i, j, k, l;

  Adder #(.width(32)) adder_1 (.a(A), .b(B), .out(add0));  // open: cin, cout
  Adder #(.width(32)) adder_2 (.a(A), .b(B), .out(add0));  // open: cin, cout
  assign a_t = A & B;  // AND_Gate and_1, 32 bits wide
  assign b_t = A | B;  // OR_Gate or_1, 32 bits wide
  assign c = A ^ B;  // XOR_Gate xor_1, 32 bits wide
  Shifter #(.width(32), .shift("lr")) shifter_1 (.in(A), .\dist (B[4:0]), .out(d));
  Shifter #(.width(32), .shift("ar")) shifter_2 (.in(A), .\dist (B[4:0]), .out(e));
  Shifter #(.width(32)) shifter_3 (.in(A), .\dist (B[4:0]), .out(f));
  Comparator #(.width(32)) comparator_1 (
    .a(A), .b(B), .gt(comparator_1_gt), .eq(comparator_1_eq), .lt(comparator_1_lt));
  Multiplier #(.width(32)) multiplier_1 (.a(A), .b(B), .out(j));  // open: cin, cout
  Multiplier #(.width(32)) multiplier_2 (.a(A), .b(B), .cout(k));  // open: out, cin
  Subtractor #(.width(32)) subtractor_1 (.a(A), .b(B), .out(l));  // open: bin, bout
  or or_2 (or_2_out, comparator_1_gt, comparator_1_eq);
  not not_1 (not_1_out, or_2_out);
  Divider #(.width(32)) divider_1 (.a(A), .b(B), .out(h), .rem(i));  // open: upper
  and and_2 (and_2_out, not_1_out, comparator_1_lt);
  Multiplexer #(.select(4), .width(32), .enable("false")) multiplexer_1 (
    .in0(add0), .in1(a_t), .in2(b_t), .in3(c), .in4(d), .in5(e), .in6(f), .in7(g), .in8(h), .in9(i),
    .in10(j), .in11(k), .in12(l), .in13(B), .out(Result), .sel(ALUSel));  // open: in14, in15
  assign g = {{31{1'b0}}, and_2_out};  // Bit_Extender bit_extender_1

  // Other names for the same wires on the sheet: m[31:0] = B

  // Notes on the sheet:
  //   INPUTS to your circuit
  //   DON'T CHANGE THE LOCATIONS OF THE INPUTS AND OUTPUTS!
  //   OUTPUT from your circuit
endmodule
